# Fritzing sketch project1 (saved by Fritzing 0.9.3b)
breadboards: 1

parts:
  Part1 = Arduino Uno (Rev3) - ICSP
  R1 = Resistor [tolerance=±5% resistance=220 package="0805 [SMD]"]
  LED1 = LEDs [package=led10mm]

nets:
  N1: Part1.D13/SCK, R1.Pin_1
  N2: Part1.GND, LED1.A
